# Fritzing sketch projectCircuitDiagram (saved by Fritzing 0.9.3b)
breadboards: 1

parts:
  Part1 = Photon
  IR1 = TSOP312.., 314.. [package=THT]
  D1 = LTE-302 [package=lte-302]
  IR2 = TSOP312.., 314.. [package=THT]
  D2 = LTE-302 [package=lte-302]
  R1 = Resistor [tolerance=±5% resistance=220 package=THT]
  R2 = Resistor [tolerance=±5% resistance=220 package=THT]
  LED1 = LED - 5mm [color="Green (560nm)" package="5 mm [THT]"]
  LED2 = LED - 5mm [color="Red (633nm)" package="5 mm [THT]"]

nets:
  GND: Part1.GND, IR1.GND, D1.C, D2.C, R1.Pin_1, R2.Pin_1
  VIN: Part1.VIN, IR1.Data, D1.A, IR2.GND, D2.A
  N1: Part1.D0, LED2.anode
  N2: Part1.D1, LED1.anode
  N3: Part1.D4, IR1.Vs
  N4: Part1.D5, IR2.Vs
  N5: R1.Pin_0, LED1.cathode
  N6: R2.Pin_0, LED2.cathode
